# Fritzing sketch esp32-sensores (saved by Fritzing 0.9.4)
perfboards: 1

parts:
  ESP1 = ESP32-DevkitC
  BME280 = BMP280
  R1 = PHOTOCELL [package=photocell]
  R2 = Resistor [tolerance=±5% resistance=10k package=THT]

nets:
  3V3: ESP1.3V3, BME280.VIN, R2.Pin_0
  N1: ESP1.IO33, R1.P$1, R2.Pin_1
  GND: ESP1.GND, BME280.GND, R1.P$2
  N2: ESP1.IO22, BME280.SCL
  N3: ESP1.IO21, BME280.SDA

custom parts:
  BMP280: Temperature Humidity Barometric presure Sensor, I2C
